# Fritzing sketch pico-tnc (saved by Fritzing 0.9.6b)
circuit board: 8.46667cm x 5.64444cm
breadboards: 1

parts:
  LED1 = LED - 5mm [color="Green (570nm)" current=0.030 package="5 mm [THT]"]
  R1 = Resistor [tolerance=±5% power=0.25 resistance=1k package=THT]
  LED2 = LED - 5mm [color="Yellow (595nm)" current=0.030 package="5 mm [THT]"]
  R2 = Resistor [tolerance=±5% power=0.25 resistance=330 package=THT]
  Q1 = NPN-Transistor [package="TO92 [THT]"]
  R3 = Resistor [tolerance=±5% power=0.25 resistance=1k package=THT]
  R4 = Resistor [tolerance=±5% power=0.25 resistance=10k package=THT]
  R5 = Resistor [tolerance=±5% power=0.25 resistance=10k package=THT]
  C1 = Ceramic Capacitor [capacitance=100nF voltage=35V package="100 mil [THT, multilayer]"]
  D1 = Rectifier Diode [part_number=1N4001 package="300 mil [THT]"]
  D2 = Rectifier Diode [part_number=1N4001 package="300 mil [THT]"]
  R6 = Resistor [tolerance=±5% power=0.25 resistance=100 package=THT]
  C2 = Ceramic Capacitor [capacitance=100nF voltage=35V package="100 mil [THT, multilayer]"]
  R7 = Resistor [tolerance=±5% power=0.25 resistance=100k package=THT]
  R8 = Resistor [tolerance=±5% power=0.25 resistance=10k package=THT]
  C3 = Ceramic Capacitor [capacitance=100nF voltage=35V package="100 mil [THT, multilayer]"]
  J1 = female pin header, 4 pins [form="♀ (female)"]
  Mod1 = Raspberry Pi Pico

nets:
  GND: LED1.cathode, LED2.cathode, Q1.E, R5.Pin_1, D2.anode, C2.0, R8.Pin_1, J1.pin3, Mod1.pin_8, Mod1.pin_28
  N1: LED1.anode, R1.Pin_0
  N2: R1.Pin_1, Mod1.pin_29
  N3: LED2.anode, R2.Pin_0
  N4: R2.Pin_1, R3.Pin_0, Mod1.pin_15
  N5: Q1.B, R3.Pin_1
  N6: Q1.C, J1.pin2
  N7: R4.Pin_0, D1.cathode, Mod1.pin_36
  N8: R4.Pin_1, R5.Pin_0, C1.0, D1.anode, D2.cathode, Mod1.pin_31
  N9: C1.1, J1.pin1
  N10: R6.Pin_0, Mod1.pin_14
  N11: R6.Pin_1, C2.1, R7.Pin_0
  N12: R7.Pin_1, R8.Pin_0, C3.0
  N13: C3.1, J1.pin4

notes:
  PTT
  Spkr+
  Mic+
  Gnd

custom parts:
  Raspberry Pi Pico: Raspberry Pi Pico. Based around the RP2040 microcontroller the Pico is a low cost microcontroller device bringing Raspberry Pi quality, cost, and easy of use to the microcontroller space. Jan 2021, Split part in to two versions: tht (this one) and SMD. This one will drill holes for a .1 in header in pcb to allow plugging in the module as well as providing pads to solder the module to the top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
